// Logisim project un0.circ as structural Verilog: 16 circuits, main circuit main
module Stepper (
  input  in_1,
  input  in_2,
  input  in_3
);

  wire and_1_out, and_2_out, and_3_out, and_4_out, nand_1_out, nand_2_out, nand_3_out, nand_4_out,
       nand_5_out, nand_6_out, nand_7_out, nand_8_out, nand_9_out, nand_10_out, nand_11_out, nand_12_out,
       nand_13_out, nand_14_out, nand_15_out, nand_16_out, nand_17_out, nand_18_out, nand_19_out,
       nand_20_out, nand_21_out, nand_22_out, nand_23_out, nand_24_out, nand_25_out, nand_26_out,
       nand_27_out, nand_28_out, nand_29_out, nand_30_out, nand_31_out, nand_32_out, nand_33_out,
       nand_34_out, nand_35_out, nand_36_out, nand_37_out, nand_38_out, nand_39_out, nand_40_out,
       nand_41_out, nand_42_out, nand_43_out, nand_44_out, nand_45_out, nand_46_out, nand_47_out,
       nand_48_out, nand_49_out, nand_50_out, nand_51_out, nand_52_out, nand_53_out, nand_54_out,
       nand_55_out, nand_56_out, nand_57_out, nand_58_out, nand_59_out, nand_60_out, nand_61_out,
       nand_62_out, nand_63_out, nand_64_out, nor_1_out, nor_2_out, or_1_out, or_2_out, or_3_out;

  nand nand_1 (nand_1_out, nand_2_out, nand_3_out, ~in_2);  // NAND_Gate
  nand nand_2 (nand_2_out, nand_1_out, nand_4_out);
  nand nand_3 (nand_3_out, in_3, ~nand_11_out);  // NAND_Gate
  nand nand_4 (nand_4_out, nand_11_out, in_3);
  nand nand_5 (nand_5_out, nand_11_out, nand_6_out);
  nand nand_6 (nand_6_out, ~or_1_out, ~in_3);  // NAND_Gate
  nand nand_7 (nand_7_out, ~in_3, or_1_out);  // NAND_Gate
  nand nand_8 (nand_8_out, nand_13_out, nand_9_out);
  nand nand_9 (nand_9_out, nand_15_out, in_3);
  nand nand_10 (nand_10_out, nand_15_out, nand_12_out);
  nand nand_11 (nand_11_out, nand_5_out, nand_7_out);
  nand nand_12 (nand_12_out, ~nand_2_out, ~in_3);  // NAND_Gate
  nand nand_13 (nand_13_out, nand_8_out, nand_14_out, ~in_2);  // NAND_Gate
  nand nand_14 (nand_14_out, in_3, ~nand_15_out);  // NAND_Gate
  nand nand_15 (nand_15_out, nand_10_out, nand_16_out);
  nand nand_16 (nand_16_out, ~in_3, nand_2_out);  // NAND_Gate
  or or_1 (or_1_out, and_1_out, and_2_out);
  nand nand_17 (nand_17_out, nand_18_out, nand_20_out);
  nand nand_18 (nand_18_out, nand_17_out, nand_19_out, ~in_2);  // NAND_Gate
  nand nand_19 (nand_19_out, in_3, ~nand_26_out);  // NAND_Gate
  nand nand_20 (nand_20_out, nand_26_out, in_3);
  nand nand_21 (nand_21_out, nand_26_out, nand_23_out);
  nand nand_22 (nand_22_out, ~in_3, nand_8_out);  // NAND_Gate
  nand nand_23 (nand_23_out, ~nand_8_out, ~in_3);  // NAND_Gate
  nor nor_1 (nor_1_out, nand_33_out, nand_24_out, nand_17_out, nand_8_out, nand_2_out);
  and and_1 (and_1_out, nor_1_out, ~in_1);  // AND_Gate
  and and_2 (and_2_out, in_1, nor_2_out);
  nor nor_2 (nor_2_out, nand_50_out, nand_40_out, nand_33_out, nand_24_out, nand_17_out, nand_8_out, nand_2_out);
  nand nand_24 (nand_24_out, nand_29_out, nand_25_out);
  nand nand_25 (nand_25_out, nand_31_out, in_3);
  nand nand_26 (nand_26_out, nand_21_out, nand_22_out);
  nand nand_27 (nand_27_out, nand_31_out, nand_28_out);
  nand nand_28 (nand_28_out, ~nand_17_out, ~in_3);  // NAND_Gate
  nand nand_29 (nand_29_out, nand_24_out, nand_30_out, ~in_2);  // NAND_Gate
  nand nand_30 (nand_30_out, in_3, ~nand_31_out);  // NAND_Gate
  nand nand_31 (nand_31_out, nand_27_out, nand_32_out);
  nand nand_32 (nand_32_out, ~in_3, nand_17_out);  // NAND_Gate
  or or_2 (or_2_out, nand_33_out, and_4_out);
  or or_3 (or_3_out, nand_40_out, and_3_out);
  and and_3 (and_3_out, nand_56_out, in_1);
  and and_4 (and_4_out, in_1, nand_50_out);
  nand nand_33 (nand_33_out, nand_34_out, nand_35_out);
  nand nand_34 (nand_34_out, nand_33_out, nand_36_out, ~in_2);  // NAND_Gate
  nand nand_35 (nand_35_out, nand_43_out, in_3);
  nand nand_36 (nand_36_out, in_3, ~nand_43_out);  // NAND_Gate
  nand nand_37 (nand_37_out, nand_43_out, nand_39_out);
  nand nand_38 (nand_38_out, ~in_3, nand_24_out);  // NAND_Gate
  nand nand_39 (nand_39_out, ~nand_24_out, ~in_3);  // NAND_Gate
  nand nand_40 (nand_40_out, nand_45_out, nand_41_out);
  nand nand_41 (nand_41_out, nand_47_out, in_3);
  nand nand_42 (nand_42_out, nand_47_out, nand_44_out);
  nand nand_43 (nand_43_out, nand_37_out, nand_38_out);
  nand nand_44 (nand_44_out, ~nand_33_out, ~in_3);  // NAND_Gate
  nand nand_45 (nand_45_out, nand_40_out, nand_46_out, ~in_2);  // NAND_Gate
  nand nand_46 (nand_46_out, in_3, ~nand_47_out);  // NAND_Gate
  nand nand_47 (nand_47_out, nand_42_out, nand_48_out);
  nand nand_48 (nand_48_out, ~in_3, nand_33_out);  // NAND_Gate
  nand nand_49 (nand_49_out, nand_50_out, nand_51_out, ~in_2);  // NAND_Gate
  nand nand_50 (nand_50_out, nand_49_out, nand_52_out);
  nand nand_51 (nand_51_out, in_3, ~nand_58_out);  // NAND_Gate
  nand nand_52 (nand_52_out, nand_58_out, in_3);
  nand nand_53 (nand_53_out, nand_58_out, nand_55_out);
  nand nand_54 (nand_54_out, ~in_3, nand_40_out);  // NAND_Gate
  nand nand_55 (nand_55_out, ~nand_40_out, ~in_3);  // NAND_Gate
  nand nand_56 (nand_56_out, nand_61_out, nand_57_out);
  nand nand_57 (nand_57_out, nand_63_out, in_3);
  nand nand_58 (nand_58_out, nand_53_out, nand_54_out);
  nand nand_59 (nand_59_out, nand_63_out, nand_60_out);
  nand nand_60 (nand_60_out, ~nand_50_out, ~in_3);  // NAND_Gate
  nand nand_61 (nand_61_out, nand_56_out, nand_62_out, ~in_2);  // NAND_Gate
  nand nand_62 (nand_62_out, in_3, ~nand_63_out);  // NAND_Gate
  nand nand_63 (nand_63_out, nand_59_out, nand_64_out);
  nand nand_64 (nand_64_out, ~in_3, nand_50_out);  // NAND_Gate
  // NOT_Gate not_1 is placed but not wired
  // NOT_Gate not_2 is placed but not wired
endmodule

module main (
  input  Flag_state_in,
  input  in_2,
  input  in_3,
  input  in_4,
  input  in_5,
  input  in_6,
  input  in_7,
  input  in_8,
  input  in_9,
  output acc2,
  output temp1,
  output out_12,
  output out_13,
  output out_14,
  output out_15,
  output out_16,
  output out_17,
  output out_18,
  output out_19,
  output out_20,
  output out_21,
  output out_22,
  output rom,
  output out_24,
  output out_25,
  output out_26,
  output z,
  output out_28,
  output IN_CLR
);

  wire clockbox_1_out_1, clockbox_1_out_2, demultiplexer_1_out1, nor_1_out, or_3_out, stepper_1_p5;
  wire [7:0] or_2_out;
  wire [8:0] demultiplexer_1_out0, demultiplexer_2_out0, demultiplexer_2_out1;
  wire [9:1] stepper_1_p4;

  assign {z, out_25, rom, out_21, out_19, out_17, out_15, out_13, temp1} = clockbox_1_out_2 ? {demultiplexer_2_out1[6], or_2_out[7:5], demultiplexer_2_out1[3], or_2_out[3], demultiplexer_2_out1[2], demultiplexer_2_out1[0], or_2_out[0]} : 9'bz;  // Controlled_Buffer controlled_buffer_1
  Pull_Resistor pull_resistor_1 (.node({z, out_25, rom, out_21, out_19, out_17, out_15, out_13, temp1}));
  or or_1 (or_2_out[5], stepper_1_p5, demultiplexer_2_out1[5], stepper_1_p4[1]);
  or or_2 (or_2_out[3], or_2_out[0], demultiplexer_2_out1[1]);
  // NOT_Gate not_1 has open pins: in=clockbox_1_out_2, out=open
  nor nor_1 (nor_1_out, in_2, in_3, in_4, in_5, in_6);
  clockbox clockbox_1 (.out_1(clockbox_1_out_1), .out_2(clockbox_1_out_2));
  Pull_Resistor pull_resistor_2 (.node(or_2_out[7]));
  Pull_Resistor pull_resistor_3 (.node(or_2_out[0]));
  // Stepper stepper_1: pin names not known; wires that end beside it: Flag_state_in, stepper_1_p4[9], or_2_out[6], stepper_1_p4[1], stepper_1_p5, or_2_out[0], or_2_out[7]
  or or_3 (or_3_out, stepper_1_p4[9], stepper_1_p5);
  Demultiplexer demultiplexer_1 (
    .out0(demultiplexer_1_out0[0]), .out1(demultiplexer_1_out1), .in(or_3_out), .sel(nor_1_out));  // open: en
  Decoder #(.select(3), .disabled(0)) decoder_1 (
    .out0(demultiplexer_1_out0[1]), .out1(demultiplexer_1_out0[2]), .out2(demultiplexer_1_out0[3]),
    .out3(demultiplexer_1_out0[4]), .out4(demultiplexer_1_out0[5]), .out5(demultiplexer_1_out0[6]),
    .out6(demultiplexer_1_out0[7]), .out7(demultiplexer_1_out0[8]), .sel({in_7, in_8, in_9}),
    .en(demultiplexer_1_out1));
  Demultiplexer #(.width(9)) demultiplexer_2 (
    .out0(demultiplexer_2_out0), .out1(demultiplexer_2_out1), .in(demultiplexer_1_out0), .sel(stepper_1_p4[9]));  // open: en
  or or_4 (stepper_1_p4[7], or_2_out[7], demultiplexer_2_out0[1]);
  Pull_Resistor pull_resistor_4 (.node({IN_CLR, out_28, out_26, out_24, out_22, out_20, out_18, out_16, out_14, out_12, acc2}));
  assign {IN_CLR, out_28, out_26, out_24, out_22, out_20, out_18, out_16, out_14, out_12, acc2} = clockbox_1_out_1 ? {demultiplexer_2_out0[3], stepper_1_p4[9], demultiplexer_2_out0[0], stepper_1_p4[7], demultiplexer_2_out0[2], demultiplexer_2_out0[4], stepper_1_p4[9], {2{or_2_out[6]}}, stepper_1_p4[1], or_2_out[0]} : 11'bz;  // Controlled_Buffer controlled_buffer_2
endmodule

module clockbox (
  output out_1,
  output out_2
);

  wire buffer_1_out, clock_1_out, clock_2_out, not_1_out;

  Clock #(.highDuration(3), .lowDuration(3)) clock_1 (.out(clock_1_out));
  Clock clock_2 (.out(clock_2_out));
  buf buffer_1 (buffer_1_out, clock_1_out);
  not not_1 (not_1_out, clock_2_out);
  and and_1 (out_1, buffer_1_out, not_1_out);
  or or_1 (out_2, buffer_1_out, not_1_out);
endmodule

module Board (
  input  flag_in,
  input  [7:0] in_2,
  output temp,
  output temp1,
  output mar,
  output ram,
  output ir,
  output iar2,
  output acc,
  output iar,
  output out,
  output in,
  output iar2_2,
  output acc_2,
  output iar_2,
  output rom,
  output ram_2,
  output acc2,
  output flag,
  output zero,
  output acc2_2,
  output IN_CLR
);

  main main_1 (
    .temp1(temp1), .out_13(ram), .out_15(iar2), .out_17(iar), .out_19(in), .out_21(acc_2), .rom(rom),
    .Flag_state_in(flag_in), .out_12(temp), .out_14(mar), .out_16(ir), .out_18(acc), .out_20(out),
    .out_22(iar2_2), .out_24(iar_2), .out_26(ram_2), .out_28(flag), .in_2(in_2[7]), .in_3(in_2[6]),
    .in_4(in_2[5]), .in_5(in_2[4]), .in_6(in_2[3]), .in_7(in_2[2]), .in_8(in_2[1]), .in_9(in_2[0]),
    .acc2(acc2_2), .out_25(acc2), .z(zero), .IN_CLR(IN_CLR));
endmodule

module enabler (
  input  in_1,
  input  in_2,
  output out_3
);

  assign out_3 = in_2 ? in_1 : 1'bz;  // Controlled_Buffer controlled_buffer_1
  Pull_Resistor pull_resistor_1 (.node(out_3));
  // AND_Gate and_1 is placed but not wired
endmodule

module CPU (
  input  [7:0] IN,
  input  IN_SET,
  output [7:0] OUT,
  output OUT_was_SET
);

  wire alu_1_carry_out, board_1_acc, board_1_acc2, board_1_acc2_2, board_1_acc_2, board_1_flag, board_1_iar,
       board_1_iar2, board_1_iar2_2, board_1_iar_2, board_1_in, board_1_in_clr, board_1_ir, board_1_mar,
       board_1_ram, board_1_ram_2, board_1_rom, board_1_temp, board_1_temp1, FLAG_q;
  wire [7:0] ACC2_q, ACC_q, alu_1_c, controlled_buffer_1_out, IAR2_q, IAR_q, IN_q, IR_q, MAR_q, rom_1_data,
       temp_1_out;

  Register IAR2 (.D(controlled_buffer_1_out), .Q(IAR2_q), .clk(board_1_iar2_2));  // open: en, clr
  Register ACC2 (.D(alu_1_c), .Q(ACC2_q), .clk(board_1_acc2_2));  // open: en, clr
  assign controlled_buffer_1_out = board_1_acc2 ? ACC2_q : 8'bz;  // Controlled_Buffer controlled_buffer_1
  ALU alu_1 (.A(controlled_buffer_1_out), .B(temp_1_out), .C(alu_1_c), .carry_out(alu_1_carry_out));
  Register MAR (.D(controlled_buffer_1_out), .Q(MAR_q), .clk(board_1_mar));  // open: en, clr
  assign controlled_buffer_1_out = board_1_iar2 ? IAR2_q : 8'bz;  // Controlled_Buffer controlled_buffer_2
  ROM #(.addrWidth(16)) rom_1 (.addr({IAR2_q, IAR_q}), .data(rom_1_data));  // open: sel
  Register ACC (.D(alu_1_c), .Q(ACC_q), .clk(board_1_acc));  // open: en, clr
  assign controlled_buffer_1_out = board_1_acc_2 ? ACC_q : 8'bz;  // Controlled_Buffer controlled_buffer_3
  Temp temp_1 (.temp1(board_1_temp1), .in(controlled_buffer_1_out), .set(board_1_temp), .out(temp_1_out));
  Register #(.width(1)) FLAG (.D(alu_1_carry_out), .Q(FLAG_q), .clk(board_1_flag));  // open: en, clr
  Register u_IN (.D(IN), .Q(IN_q), .clk(IN_SET), .clr(board_1_in_clr));  // open: en
  assign controlled_buffer_1_out = board_1_in ? IN_q : 8'bz;  // Controlled_Buffer controlled_buffer_4
  Register u_OUT (.D(controlled_buffer_1_out), .Q(OUT), .clk(OUT_was_SET));  // open: en, clr
  Pull_Resistor pull_resistor_1 (.node(controlled_buffer_1_out));
  RAM ram_1 (.addr(MAR_q), .data(controlled_buffer_1_out), .clk(board_1_ram_2), .ld(board_1_ram));  // open: sel, clr
  assign controlled_buffer_1_out = board_1_iar ? IAR_q : 8'bz;  // Controlled_Buffer controlled_buffer_5
  Register IAR (.D(controlled_buffer_1_out), .Q(IAR_q), .clk(board_1_iar_2));  // open: en, clr
  assign controlled_buffer_1_out = board_1_rom ? rom_1_data : 8'bz;  // Controlled_Buffer controlled_buffer_6
  Board board_1 (
    .temp1(board_1_temp1), .ram(board_1_ram), .iar2(board_1_iar2), .iar(board_1_iar), .in(board_1_in),
    .acc_2(board_1_acc_2), .rom(board_1_rom), .acc2(board_1_acc2), .temp(board_1_temp), .mar(board_1_mar),
    .ir(board_1_ir), .acc(board_1_acc), .out(OUT_was_SET), .iar2_2(board_1_iar2_2), .iar_2(board_1_iar_2),
    .ram_2(board_1_ram_2), .flag(board_1_flag), .acc2_2(board_1_acc2_2), .flag_in(FLAG_q), .in_2(IR_q),
    .IN_CLR(board_1_in_clr));  // open: zero
  Register IR (.D(controlled_buffer_1_out), .Q(IR_q), .clk(board_1_ir));  // open: en, clr
  Hex_Digit_Display hex_digit_display_1 (.value(OUT[7:4]));  // open: dp
  Hex_Digit_Display hex_digit_display_2 (.value(OUT[3:0]));  // open: dp

  // Notes on the sheet:
  //   contents of rom_1 (hex, n*v repeats v):
  //   4 4 0 10 5 11 5 10 3 15*4
endmodule

module ALU (
  input  [7:0] A,
  input  [7:0] B,
  output [7:0] C,
  output carry_out
);

  Subtractor subtractor_1 (.a(A), .b(B), .out(C), .bout(carry_out));  // open: bin

  // Notes on the sheet:
  //   Note: A-B=C
endmodule

// TMP
module Temp (
  input  temp1,
  input  [7:0] in,
  input  set,
  output [7:0] out
);

  wire [7:0] pull_resistor_1_node, register_1_q;

  Register register_1 (.D(in), .Q(register_1_q), .clk(set));  // open: en, clr
  Pull_Resistor pull_resistor_1 (.node(pull_resistor_1_node));
  assign pull_resistor_1_node = temp1 ? {8{1'b1}} : 8'bz;  // Controlled_Buffer controlled_buffer_1
  assign out = pull_resistor_1_node | register_1_q;  // OR_Gate or_1, 8 bits wide
endmodule

module safe_stop (
  input  e,
  input  s,
  input  stop,
  input  e_2,
  input  s_2,
  output out_6,
  output out_7
);

  wire and_1_out, nor_1_out, or_1_out;

  Multiplexer multiplexer_1 (.in0(e), .in1(e_2), .out(out_6), .sel(and_1_out));  // open: en
  nor nor_1 (nor_1_out, e, s);
  and and_1 (and_1_out, stop, or_1_out);
  or or_1 (or_1_out, nor_1_out, and_1_out);
  Multiplexer multiplexer_2 (.in0(s), .in1(s_2), .out(out_7), .sel(and_1_out));  // open: en
endmodule

module panel (
  input  [7:0] switch_register,
  input  set_in,
  input  halt,
  input  [2:0] ereg,
  input  [2:0] sreg,
  input  set,
  input  step,
  output [7:0] DATA_OUT,
  output [5:0] Step_2,
  output [7:0] BUS_MAR_MAR2
);

  wire demultiplexer_1_out8, demultiplexer_1_out9, demultiplexer_1_out10, demultiplexer_1_out11,
       demultiplexer_1_out12, demultiplexer_1_out13, demultiplexer_1_out14, demultiplexer_1_out15,
       demultiplexer_2_out8, demultiplexer_2_out9, demultiplexer_2_out10, demultiplexer_2_out11,
       demultiplexer_2_out12, demultiplexer_2_out13, demultiplexer_2_out14, demultiplexer_2_out15;
  wire [1:0] demultiplexer_1_out6;
  wire [3:0] register_1_q;
  wire [5:0] demultiplexer_1_out0;
  wire [7:0] demultiplexer_2_out0, undriven, undriven_2, undriven_3;

  Demultiplexer #(.select(4)) demultiplexer_1 (
    .out0(demultiplexer_1_out0[0]), .out1(demultiplexer_1_out0[1]), .out2(demultiplexer_1_out0[2]),
    .out3(demultiplexer_1_out0[3]), .out4(demultiplexer_1_out0[4]), .out5(demultiplexer_1_out0[5]),
    .out6(demultiplexer_1_out6[0]), .out7(demultiplexer_1_out6[1]), .out8(demultiplexer_1_out8),
    .out9(demultiplexer_1_out9), .out10(demultiplexer_1_out10), .out11(demultiplexer_1_out11),
    .out12(demultiplexer_1_out12), .out13(demultiplexer_1_out13), .out14(demultiplexer_1_out14),
    .out15(demultiplexer_1_out15), .in(1'b1), .sel({1'b0, ereg}));  // open: en
  Multiplexer #(.select(2), .width(8)) multiplexer_1 (
    .in0(undriven), .in1(undriven_2), .in2(undriven_3), .out(BUS_MAR_MAR2), .sel(demultiplexer_1_out6));  // open: in3, en
  Demultiplexer #(.select(4)) demultiplexer_2 (
    .out0(demultiplexer_2_out0[0]), .out1(demultiplexer_2_out0[1]), .out2(demultiplexer_2_out0[2]),
    .out3(demultiplexer_2_out0[3]), .out4(demultiplexer_2_out0[4]), .out5(demultiplexer_2_out0[5]),
    .out6(demultiplexer_2_out0[6]), .out7(demultiplexer_2_out0[7]), .out8(demultiplexer_2_out8),
    .out9(demultiplexer_2_out9), .out10(demultiplexer_2_out10), .out11(demultiplexer_2_out11),
    .out12(demultiplexer_2_out12), .out13(demultiplexer_2_out13), .out14(demultiplexer_2_out14),
    .out15(demultiplexer_2_out15), .in(1'b1), .sel(register_1_q));  // open: en
  Register #(.width(4)) register_1 (.D({1'b0, sreg}), .Q(register_1_q), .clk(set));  // open: en, clr

  // Notes on the sheet:
  //   22
  //   40
  //   18
  //   47 connections
  //   25 in , 22 out
  //   38
  //   63
  //   25
endmodule

module step (
  input  in_1,
  input  in_2,
  input  stop,
  input  e,
  input  s,
  output out_6,
  output out_7,
  output out_8,
  output out_9
);

  wire and_1_out, clock_1_out, controlled_buffer_1_out, nor_1_out, not_1_out, or_1_out, register_1_q,
       t_ff_1_q;

  assign controlled_buffer_1_out = in_1 ? in_1 : 1'bz;  // Controlled_Buffer controlled_buffer_1
  assign controlled_buffer_1_out = not_1_out ? clock_1_out : 1'bz;  // Controlled_Buffer controlled_buffer_2
  Clock clock_1 (.out(clock_1_out));
  not not_1 (not_1_out, in_2);
  T_Flip_Flop t_ff_1 (.clk(controlled_buffer_1_out), .T(1'b1), .Q(t_ff_1_q));  // open: Qn, preset, reset, en
  Multiplexer multiplexer_1 (.in0(out_7), .in1(e), .out(out_8), .sel(and_1_out));  // open: en
  Pull_Resistor pull_resistor_1 (.node(controlled_buffer_1_out));
  nand nand_1 (out_7, controlled_buffer_1_out, t_ff_1_q);
  assign out_6 = out_7 ? controlled_buffer_1_out : 1'bz;  // Controlled_Buffer controlled_buffer_3
  Pull_Resistor pull_resistor_2 (.node(out_6));
  nor nor_1 (nor_1_out, out_7, out_6);
  or or_1 (or_1_out, nor_1_out, register_1_q);
  and and_1 (and_1_out, stop, or_1_out);
  Multiplexer multiplexer_2 (.in0(out_6), .in1(s), .out(out_9), .sel(and_1_out));  // open: en
  Register #(.width(1)) register_1 (.D(and_1_out), .Q(register_1_q), .clk(and_1_out));  // open: en, clr
endmodule

module clock (
  input  in_1,
  input  in_2,
  input  in_3,
  input  in_4,
  output out_5,
  output out_6
);

  wire and_1_out, buffer_1_out, buffer_2_out, clock_1_out, controlled_buffer_1_out, n8_1_out_2, not_1_out,
       pull_resistor_2_node, t_ff_1_q, t_ff_1_qn, t_ff_2_qn, t_ff_3_q, t_ff_4_qn, xnor_1_out;

  xnor xnor_1 (xnor_1_out, in_1, t_ff_3_q);
  assign controlled_buffer_1_out = xnor_1_out ? clock_1_out : 1'bz;  // Controlled_Buffer controlled_buffer_1
  Clock clock_1 (.out(clock_1_out));
  Pull_Resistor pull_resistor_1 (.node(controlled_buffer_1_out));
  T_Flip_Flop t_ff_1 (
    .clk(controlled_buffer_1_out), .T(1'b1), .Q(t_ff_1_q), .Qn(t_ff_1_qn));  // open: preset, reset, en
  T_Flip_Flop t_ff_2 (.clk(t_ff_1_qn), .T(1'b1), .Qn(t_ff_2_qn));  // open: Q, preset, reset, en
  T_Flip_Flop t_ff_3 (.clk(t_ff_2_qn), .T(1'b1), .Q(t_ff_3_q));  // open: Qn, preset, reset, en
  Pull_Resistor pull_resistor_2 (.node(pull_resistor_2_node));
  assign pull_resistor_2_node = t_ff_1_q ? t_ff_1_q : 1'bz;  // Controlled_Buffer controlled_buffer_2
  not not_1 (not_1_out, in_2);
  assign pull_resistor_2_node = not_1_out ? clock_1_out : 1'bz;  // Controlled_Buffer controlled_buffer_3
  _8 u_8_1 (.in_1(in_3), .out_2(n8_1_out_2));
  assign pull_resistor_2_node = n8_1_out_2 ? n8_1_out_2 : 1'bz;  // Controlled_Buffer controlled_buffer_4
  buf buffer_1 (buffer_1_out, pull_resistor_2_node);
  buf buffer_2 (buffer_2_out, buffer_1_out);
  T_Flip_Flop t_ff_4 (.clk(pull_resistor_2_node), .T(1'b1), .Qn(t_ff_4_qn));  // open: Q, preset, reset, en
  buf buffer_3 (out_5, buffer_2_out);
  nand nand_1 (out_6, buffer_2_out, t_ff_4_qn);
  and and_1 (and_1_out, out_5, out_6);
  Counter counter_1 (.count(1'b1), .clk(and_1_out), .clr(in_4));  // open: load, D, Q, carry
endmodule

module _8 (
  input  in_1,
  output out_2
);

  wire clock_1_out, controlled_buffer_1_out, t_ff_1_qn, t_ff_2_qn, t_ff_3_qn, t_ff_4_qn, t_ff_5_qn, t_ff_6_q,
       xnor_1_out;

  xnor xnor_1 (xnor_1_out, in_1, t_ff_6_q);
  Clock clock_1 (.out(clock_1_out));
  assign controlled_buffer_1_out = xnor_1_out ? clock_1_out : 1'bz;  // Controlled_Buffer controlled_buffer_1
  Pull_Resistor pull_resistor_1 (.node(controlled_buffer_1_out));
  T_Flip_Flop t_ff_1 (.clk(controlled_buffer_1_out), .T(1'b1), .Q(out_2), .Qn(t_ff_1_qn));  // open: preset, reset, en
  T_Flip_Flop t_ff_2 (.clk(t_ff_1_qn), .T(1'b1), .Qn(t_ff_2_qn));  // open: Q, preset, reset, en
  T_Flip_Flop t_ff_3 (.clk(t_ff_2_qn), .T(1'b1), .Qn(t_ff_3_qn));  // open: Q, preset, reset, en
  T_Flip_Flop t_ff_4 (.clk(t_ff_3_qn), .T(1'b1), .Qn(t_ff_4_qn));  // open: Q, preset, reset, en
  T_Flip_Flop t_ff_5 (.clk(t_ff_4_qn), .T(1'b1), .Qn(t_ff_5_qn));  // open: Q, preset, reset, en
  T_Flip_Flop t_ff_6 (.clk(t_ff_5_qn), .T(1'b1), .Q(t_ff_6_q));  // open: Qn, preset, reset, en
endmodule

module scematic (
  input  Flag_state_in,
  input  in_2,
  input  in_3,
  input  in_4,
  input  in_5,
  input  in_6,
  input  in_7,
  input  in_8,
  input  in_9,
  input  in_10,
  output out_11
);

  wire and_1_out, and_2_out, and_3_out, and_4_out, and_5_out, and_6_out, and_7_out, and_8_out, and_9_out,
       and_10_out, and_11_out, and_12_out, and_13_out, and_14_out, and_15_out, and_16_out, and_17_out,
       and_18_out, and_19_out, and_20_out, and_21_out, and_22_out, and_23_out, and_24_out, and_25_out,
       and_26_out, and_27_out, and_28_out, and_29_out, and_30_out, and_31_out, and_32_out, and_33_out,
       and_34_out, and_39_out, and_40_out, and_41_out, and_42_out, and_44_out, and_45_out, and_48_out,
       and_49_out, and_50_out, and_51_out, and_52_out, and_53_out, and_54_out, and_55_out, and_56_out,
       and_57_out, and_58_out, and_59_out, and_60_out, buffer_1_out, buffer_2_out, buffer_3_out,
       buffer_4_out, buffer_5_out, buffer_6_out, clock_1_out, controlled_buffer_1_out, nand_1_out,
       nand_2_out, nand_3_out, nand_4_out, nand_5_out, nand_6_out, nand_7_out, nand_8_out, nand_9_out,
       nand_10_out, nand_11_out, nand_12_out, nand_13_out, nand_14_out, nand_15_out, nand_16_out,
       nand_17_out, nand_18_out, nand_19_out, nand_20_out, nand_21_out, nand_22_out, nand_23_out,
       nand_24_out, nand_25_out, nand_26_out, nand_27_out, nand_28_out, nand_29_out, nand_30_out,
       nand_31_out, nand_32_out, nand_33_out, nand_34_out, nand_35_out, nand_37_out, nand_38_out,
       nand_39_out, nand_40_out, nand_41_out, nand_42_out, nand_43_out, nand_44_out, nand_45_out,
       nand_46_out, nand_47_out, nand_48_out, nand_49_out, nand_50_out, nand_51_out, nand_52_out,
       nand_53_out, nand_54_out, nand_55_out, nand_56_out, nand_57_out, nand_58_out, nand_59_out,
       nand_60_out, nand_61_out, nand_62_out, nand_63_out, nand_64_out, nand_65_out, nand_66_out,
       nand_67_out, nand_68_out, nand_69_out, nand_70_out, nand_71_out, nand_72_out, nand_73_out, nor_1_out,
       nor_2_out, nor_3_out, not_2_out, not_3_out, not_4_out, not_5_out, or_1_out, or_2_out, or_3_out,
       or_4_out, or_5_out, or_6_out, or_7_out;

  // NOT_Gate not_1 is placed but not wired
  and and_1 (and_1_out, nand_41_out, or_5_out);
  and and_2 (and_2_out, nand_41_out, and_39_out);
  and and_3 (and_3_out, nand_41_out, and_41_out);
  and and_4 (and_4_out, nand_41_out, or_2_out);
  and and_5 (and_5_out, nand_41_out, and_42_out);
  and and_6 (and_6_out, nand_41_out, or_1_out);
  and and_7 (and_7_out, nand_41_out, nand_2_out);
  and and_8 (and_8_out, nand_41_out, or_6_out);
  and and_9 (and_9_out, nand_41_out, and_45_out);
  or or_1 (or_1_out, nand_30_out, and_44_out, nand_8_out);
  or or_2 (or_2_out, or_5_out, and_40_out);
  and and_10 (and_10_out, nor_1_out, ~Flag_state_in);  // AND_Gate
  and and_11 (and_11_out, Flag_state_in, nor_2_out);
  or or_3 (or_3_out, and_10_out, and_11_out);
  not not_2 (not_2_out, nand_41_out);
  nor nor_1 (nor_1_out, or_5_out, nand_30_out, nand_22_out, nand_8_out, nand_2_out);
  nor nor_2 (nor_2_out, nand_59_out, or_6_out, or_5_out, nand_30_out, nand_22_out, nand_8_out, nand_2_out);
  nand nand_1 (nand_1_out, nand_2_out, nand_4_out, ~in_2);  // NAND_Gate
  nand nand_2 (nand_2_out, nand_1_out, nand_3_out);
  nand nand_3 (nand_3_out, nand_10_out, not_2_out);
  nand nand_4 (nand_4_out, not_2_out, ~nand_10_out);  // NAND_Gate
  nand nand_5 (nand_5_out, nand_10_out, nand_6_out);
  nand nand_6 (nand_6_out, ~or_3_out, ~not_2_out);  // NAND_Gate
  nand nand_7 (nand_7_out, ~not_2_out, or_3_out);  // NAND_Gate
  nand nand_8 (nand_8_out, nand_13_out, nand_9_out);
  nand nand_9 (nand_9_out, nand_15_out, not_2_out);
  nand nand_10 (nand_10_out, nand_5_out, nand_7_out);
  nand nand_11 (nand_11_out, nand_15_out, nand_12_out);
  nand nand_12 (nand_12_out, ~nand_2_out, ~not_2_out);  // NAND_Gate
  or or_4 (or_4_out, nand_30_out, nand_22_out);
  nor nor_3 (nor_3_out, in_3, in_4, in_5, in_6, in_7);
  buf buffer_1 (buffer_1_out, clock_1_out);
  Clock clock_1 (.out(clock_1_out));
  nand nand_13 (nand_13_out, nand_8_out, nand_14_out, ~in_2);  // NAND_Gate
  nand nand_14 (nand_14_out, not_2_out, ~nand_15_out);  // NAND_Gate
  nand nand_15 (nand_15_out, nand_11_out, nand_16_out);
  nand nand_16 (nand_16_out, ~not_2_out, nand_2_out);  // NAND_Gate
  and and_12 (and_12_out, ~nor_3_out, or_4_out);  // AND_Gate
  and and_13 (and_13_out, nor_3_out, or_4_out);
  not not_3 (not_3_out, in_8);
  not not_4 (not_4_out, in_9);
  not not_5 (not_5_out, in_10);
  buf buffer_2 (buffer_2_out, buffer_3_out);
  buf buffer_3 (buffer_3_out, buffer_5_out);
  buf buffer_4 (buffer_4_out, buffer_1_out);
  buf buffer_5 (buffer_5_out, buffer_4_out);
  nand nand_17 (nand_17_out, nand_18_out, nand_20_out);
  nand nand_18 (nand_18_out, ~out_11, ~clock_1_out);  // NAND_Gate
  nand nand_19 (nand_19_out, ~clock_1_out, out_11);  // NAND_Gate
  nand nand_20 (nand_20_out, nand_19_out, nand_17_out);
  nand nand_21 (nand_21_out, nand_22_out, nand_23_out, ~in_2);  // NAND_Gate
  nand nand_22 (nand_22_out, nand_21_out, nand_24_out);
  nand nand_23 (nand_23_out, not_2_out, ~nand_32_out);  // NAND_Gate
  nand nand_24 (nand_24_out, nand_32_out, not_2_out);
  nand nand_25 (nand_25_out, nand_32_out, nand_26_out);
  nand nand_26 (nand_26_out, ~nand_8_out, ~not_2_out);  // NAND_Gate
  nand nand_27 (nand_27_out, ~not_2_out, nand_8_out);  // NAND_Gate
  and and_14 (and_14_out, not_5_out, not_4_out, not_3_out);
  and and_15 (and_15_out, in_10, not_4_out, not_3_out);
  and and_16 (and_16_out, not_5_out, in_9, not_3_out);
  and and_17 (and_17_out, in_10, in_9, not_3_out);
  and and_18 (and_18_out, not_5_out, not_4_out, in_8);
  and and_19 (and_19_out, in_10, not_4_out, in_8);
  and and_20 (and_20_out, not_5_out, in_9, in_8);
  and and_21 (and_21_out, in_10, in_9, in_8);
  buf buffer_6 (buffer_6_out, buffer_2_out);
  nand nand_28 (nand_28_out, nand_20_out, clock_1_out);
  nand nand_29 (nand_29_out, clock_1_out, ~nand_20_out);  // NAND_Gate
  nand nand_30 (nand_30_out, nand_37_out, nand_31_out);
  nand nand_31 (nand_31_out, nand_39_out, not_2_out);
  nand nand_32 (nand_32_out, nand_25_out, nand_27_out);
  nand nand_33 (nand_33_out, nand_39_out, nand_34_out);
  nand nand_34 (nand_34_out, ~nand_22_out, ~not_2_out);  // NAND_Gate
  and and_22 (and_22_out, and_14_out, and_13_out);
  and and_23 (and_23_out, and_15_out, and_13_out);
  and and_24 (and_24_out, and_16_out, and_13_out);
  and and_25 (and_25_out, and_17_out, and_13_out);
  and and_26 (and_26_out, and_18_out, and_13_out);
  and and_27 (and_27_out, and_19_out, and_13_out);
  and and_28 (and_28_out, and_20_out, and_13_out);
  and and_29 (and_29_out, and_21_out, and_13_out);
  nand nand_35 (nand_35_out, out_11, nand_28_out);
  nand nand_36 (out_11, nand_35_out, ~in_2, nand_29_out);  // NAND_Gate
  or or_5 (or_5_out, and_48_out, nand_43_out);
  nand nand_37 (nand_37_out, nand_30_out, nand_38_out, ~in_2);  // NAND_Gate
  nand nand_38 (nand_38_out, not_2_out, ~nand_39_out);  // NAND_Gate
  nand nand_39 (nand_39_out, nand_33_out, nand_40_out);
  nand nand_40 (nand_40_out, ~not_2_out, nand_22_out);  // NAND_Gate
  assign controlled_buffer_1_out = nand_41_out ? buffer_6_out : 1'bz;  // Controlled_Buffer controlled_buffer_1
  Pull_Resistor pull_resistor_1 (.node(controlled_buffer_1_out));
  nand nand_41 (nand_41_out, buffer_6_out, nand_35_out);
  nand nand_42 (nand_42_out, nand_43_out, nand_44_out, ~in_2);  // NAND_Gate
  nand nand_43 (nand_43_out, nand_42_out, nand_45_out);
  nand nand_44 (nand_44_out, not_2_out, ~nand_51_out);  // NAND_Gate
  nand nand_45 (nand_45_out, nand_51_out, not_2_out);
  nand nand_46 (nand_46_out, nand_51_out, nand_48_out);
  nand nand_47 (nand_47_out, ~not_2_out, nand_30_out);  // NAND_Gate
  nand nand_48 (nand_48_out, ~nand_30_out, ~not_2_out);  // NAND_Gate
  and and_30 (and_30_out, ~nand_22_out, and_12_out);  // AND_Gate
  and and_31 (and_31_out, ~nand_22_out, and_22_out);  // AND_Gate
  and and_32 (and_32_out, ~nand_22_out, and_23_out);  // AND_Gate
  and and_33 (and_33_out, ~nand_22_out, and_24_out);  // AND_Gate
  and and_34 (and_34_out, ~nand_22_out, and_25_out);  // AND_Gate
  // AND_Gate and_35 has open pins: in0=nand_22_out, in1=and_26_out, out=open
  // AND_Gate and_36 has open pins: in0=nand_22_out, in1=and_27_out, out=open
  // AND_Gate and_37 has open pins: in0=nand_22_out, in1=and_28_out, out=open
  // AND_Gate and_38 has open pins: in0=nand_22_out, in1=and_29_out, out=open
  and and_39 (and_39_out, nand_22_out, and_12_out);
  and and_40 (and_40_out, nand_22_out, and_22_out);
  and and_41 (and_41_out, nand_22_out, and_23_out);
  and and_42 (and_42_out, nand_22_out, and_24_out);
  // AND_Gate and_43 has open pins: in0=nand_22_out, in1=and_25_out, out=open
  and and_44 (and_44_out, nand_22_out, and_26_out);
  and and_45 (and_45_out, nand_22_out, and_27_out);
  // AND_Gate and_46 has open pins: in0=nand_22_out, in1=and_28_out, out=open
  // AND_Gate and_47 has open pins: in0=nand_22_out, in1=and_29_out, out=open
  or or_6 (or_6_out, and_49_out, nand_49_out);
  nand nand_49 (nand_49_out, nand_54_out, nand_50_out);
  nand nand_50 (nand_50_out, nand_56_out, not_2_out);
  nand nand_51 (nand_51_out, nand_46_out, nand_47_out);
  nand nand_52 (nand_52_out, nand_56_out, nand_53_out);
  nand nand_53 (nand_53_out, ~nand_43_out, ~not_2_out);  // NAND_Gate
  and and_48 (and_48_out, Flag_state_in, nand_59_out);
  nand nand_54 (nand_54_out, nand_49_out, nand_55_out, ~in_2);  // NAND_Gate
  nand nand_55 (nand_55_out, not_2_out, ~nand_56_out);  // NAND_Gate
  nand nand_56 (nand_56_out, nand_52_out, nand_57_out);
  nand nand_57 (nand_57_out, ~not_2_out, nand_43_out);  // NAND_Gate
  nand nand_58 (nand_58_out, nand_59_out, nand_60_out, ~in_2);  // NAND_Gate
  nand nand_59 (nand_59_out, nand_58_out, nand_61_out);
  nand nand_60 (nand_60_out, not_2_out, ~nand_68_out);  // NAND_Gate
  nand nand_61 (nand_61_out, nand_68_out, not_2_out);
  nand nand_62 (nand_62_out, nand_68_out, nand_64_out);
  nand nand_63 (nand_63_out, ~not_2_out, nand_49_out);  // NAND_Gate
  nand nand_64 (nand_64_out, ~nand_49_out, ~not_2_out);  // NAND_Gate
  and and_49 (and_49_out, Flag_state_in, nand_65_out);
  nand nand_65 (nand_65_out, nand_70_out, nand_66_out);
  nand nand_66 (nand_66_out, nand_72_out, not_2_out);
  nand nand_67 (nand_67_out, nand_72_out, nand_69_out);
  nand nand_68 (nand_68_out, nand_62_out, nand_63_out);
  nand nand_69 (nand_69_out, ~nand_59_out, ~not_2_out);  // NAND_Gate
  nand nand_70 (nand_70_out, nand_65_out, nand_71_out, ~in_2);  // NAND_Gate
  nand nand_71 (nand_71_out, not_2_out, ~nand_72_out);  // NAND_Gate
  nand nand_72 (nand_72_out, nand_67_out, nand_73_out);
  nand nand_73 (nand_73_out, ~not_2_out, nand_59_out);  // NAND_Gate
  or or_7 (or_7_out, or_6_out, and_31_out);
  and and_50 (and_50_out, controlled_buffer_1_out, or_5_out);
  and and_51 (and_51_out, controlled_buffer_1_out, nand_8_out);
  and and_52 (and_52_out, controlled_buffer_1_out, nand_2_out);
  and and_53 (and_53_out, controlled_buffer_1_out, nand_2_out);
  and and_54 (and_54_out, controlled_buffer_1_out, nand_22_out);
  and and_55 (and_55_out, controlled_buffer_1_out, and_34_out);
  and and_56 (and_56_out, controlled_buffer_1_out, and_32_out);
  and and_57 (and_57_out, controlled_buffer_1_out, or_7_out);
  and and_58 (and_58_out, controlled_buffer_1_out, and_30_out);
  and and_59 (and_59_out, controlled_buffer_1_out, nand_22_out);
  and and_60 (and_60_out, controlled_buffer_1_out, and_33_out);
  // NOT_Gate not_6 is placed but not wired
  // NOT_Gate not_7 is placed but not wired
  // NOT_Gate not_8 is placed but not wired
  // NOT_Gate not_9 is placed but not wired
endmodule

module d_flip_flop (
  input  in_1,
  input  in_2,
  input  in_3,
  input  in_4,
  input  in_5,
  input  in_6,
  input  in_7,
  input  in_8,
  input  in_9,
  output out_10,
  output out_11,
  output out_12,
  output out_13,
  output out_14,
  output out_15,
  output out_16,
  output out_17,
  output out_18
);

  wire nand_1_out, nand_2_out, nand_3_out, nand_4_out, nand_5_out, nand_6_out, nand_7_out, nand_8_out,
       nand_9_out, nand_10_out, nand_11_out, nand_12_out, nand_13_out, nand_14_out, nand_15_out, nand_16_out,
       nand_17_out, nand_18_out, nand_19_out, nand_20_out, nand_21_out, nand_22_out, nand_23_out,
       nand_24_out, nand_25_out, nand_26_out, nand_27_out, nand_28_out, nand_29_out, nand_30_out,
       nand_31_out, nand_32_out, nand_34_out, nand_35_out, nand_36_out, nand_38_out, nand_39_out,
       nand_40_out, nand_42_out, nand_43_out, nand_44_out, nand_46_out, nand_47_out, nand_48_out,
       nand_50_out, nand_51_out, nand_52_out, nand_54_out, nand_55_out, nand_56_out, nand_58_out,
       nand_59_out, nand_60_out, nand_62_out, nand_63_out, nand_64_out, nand_65_out, nand_66_out,
       nand_67_out, nand_68_out, nand_69_out, nand_70_out, nand_71_out, nand_72_out, nand_73_out,
       nand_74_out, nand_75_out, nand_76_out, nand_77_out, nand_78_out, nand_79_out, nand_81_out,
       nand_82_out, nand_83_out, nand_84_out, nand_85_out, nand_86_out, nand_87_out, nand_88_out,
       nand_89_out, nand_90_out, nand_91_out, nand_92_out, nand_93_out, nand_94_out, nand_95_out,
       nand_96_out, nand_97_out, nand_98_out, nand_99_out, nand_100_out, nand_101_out, nand_102_out,
       nand_103_out, nand_104_out, nand_105_out, nand_106_out, nand_107_out, nand_108_out, nand_109_out,
       nand_110_out, nand_111_out, nand_112_out, nand_113_out, nand_114_out, nand_115_out, nand_116_out,
       nand_117_out, nand_118_out, nand_119_out, nand_120_out, nand_121_out, nand_122_out, nand_123_out,
       nand_124_out, nand_125_out, nand_126_out, nand_127_out, nand_128_out, nand_129_out, nand_130_out,
       nand_131_out, nand_132_out, nand_133_out, nand_134_out, nand_135_out, nand_136_out, or_1_out, or_2_out;

  or or_1 (or_1_out, in_6, out_18);
  nand nand_1 (nand_1_out, nand_2_out, nand_4_out);
  nand nand_2 (nand_2_out, ~or_1_out, ~in_2);  // NAND_Gate
  nand nand_3 (nand_3_out, ~in_2, or_1_out);  // NAND_Gate
  nand nand_4 (nand_4_out, nand_3_out, nand_1_out);
  nand nand_5 (nand_5_out, nand_6_out, nand_8_out);
  nand nand_6 (nand_6_out, ~out_10, ~in_2);  // NAND_Gate
  nand nand_7 (nand_7_out, ~in_2, out_10);  // NAND_Gate
  nand nand_8 (nand_8_out, nand_7_out, nand_5_out);
  nand nand_9 (nand_9_out, nand_10_out, nand_12_out);
  nand nand_10 (nand_10_out, ~out_12, ~in_2);  // NAND_Gate
  nand nand_11 (nand_11_out, ~in_2, out_12);  // NAND_Gate
  nand nand_12 (nand_12_out, nand_11_out, nand_9_out);
  nand nand_13 (nand_13_out, nand_14_out, nand_16_out);
  nand nand_14 (nand_14_out, ~out_13, ~in_2);  // NAND_Gate
  nand nand_15 (nand_15_out, ~in_2, out_13);  // NAND_Gate
  nand nand_16 (nand_16_out, nand_15_out, nand_13_out);
  nand nand_17 (nand_17_out, nand_18_out, nand_20_out);
  nand nand_18 (nand_18_out, ~out_14, ~in_2);  // NAND_Gate
  nand nand_19 (nand_19_out, ~in_2, out_14);  // NAND_Gate
  nand nand_20 (nand_20_out, nand_19_out, nand_17_out);
  nand nand_21 (nand_21_out, nand_22_out, nand_24_out);
  nand nand_22 (nand_22_out, ~out_15, ~in_2);  // NAND_Gate
  nand nand_23 (nand_23_out, ~in_2, out_15);  // NAND_Gate
  nand nand_24 (nand_24_out, nand_23_out, nand_21_out);
  nand nand_25 (nand_25_out, nand_26_out, nand_28_out);
  nand nand_26 (nand_26_out, ~out_16, ~in_2);  // NAND_Gate
  nand nand_27 (nand_27_out, ~in_2, out_16);  // NAND_Gate
  nand nand_28 (nand_28_out, nand_27_out, nand_25_out);
  nand nand_29 (nand_29_out, nand_30_out, nand_32_out);
  nand nand_30 (nand_30_out, ~out_17, ~in_2);  // NAND_Gate
  nand nand_31 (nand_31_out, ~in_2, out_17);  // NAND_Gate
  nand nand_32 (nand_32_out, nand_31_out, nand_29_out);
  nand nand_33 (out_10, nand_36_out, nand_34_out);
  nand nand_34 (nand_34_out, nand_4_out, in_2);
  nand nand_35 (nand_35_out, in_2, ~nand_4_out);  // NAND_Gate
  nand nand_36 (nand_36_out, out_10, ~in_1, nand_35_out);  // NAND_Gate
  nand nand_37 (out_12, nand_40_out, nand_38_out);
  nand nand_38 (nand_38_out, nand_8_out, in_2);
  nand nand_39 (nand_39_out, in_2, ~nand_8_out);  // NAND_Gate
  nand nand_40 (nand_40_out, out_12, ~in_1, nand_39_out);  // NAND_Gate
  nand nand_41 (out_13, nand_43_out, nand_42_out);
  nand nand_42 (nand_42_out, nand_12_out, in_2);
  nand nand_43 (nand_43_out, out_13, ~in_1, nand_44_out);  // NAND_Gate
  nand nand_44 (nand_44_out, in_2, ~nand_12_out);  // NAND_Gate
  nand nand_45 (out_14, nand_47_out, nand_46_out);
  nand nand_46 (nand_46_out, nand_16_out, in_2);
  nand nand_47 (nand_47_out, out_14, ~in_1, nand_48_out);  // NAND_Gate
  nand nand_48 (nand_48_out, in_2, ~nand_16_out);  // NAND_Gate
  nand nand_49 (out_15, nand_52_out, nand_50_out);
  nand nand_50 (nand_50_out, nand_20_out, in_2);
  nand nand_51 (nand_51_out, in_2, ~nand_20_out);  // NAND_Gate
  nand nand_52 (nand_52_out, out_15, ~in_1, nand_51_out);  // NAND_Gate
  nand nand_53 (out_16, nand_55_out, nand_54_out);
  nand nand_54 (nand_54_out, nand_24_out, in_2);
  nand nand_55 (nand_55_out, out_16, ~in_1, nand_56_out);  // NAND_Gate
  nand nand_56 (nand_56_out, in_2, ~nand_24_out);  // NAND_Gate
  nand nand_57 (out_17, nand_60_out, nand_58_out);
  nand nand_58 (nand_58_out, nand_28_out, in_2);
  nand nand_59 (nand_59_out, in_2, ~nand_28_out);  // NAND_Gate
  nand nand_60 (nand_60_out, out_17, ~in_1, nand_59_out);  // NAND_Gate
  nand nand_61 (out_18, nand_64_out, nand_62_out);
  nand nand_62 (nand_62_out, nand_32_out, in_2);
  nand nand_63 (nand_63_out, in_2, ~nand_32_out);  // NAND_Gate
  nand nand_64 (nand_64_out, out_18, ~in_1, nand_63_out);  // NAND_Gate
  nand nand_65 (nand_65_out, nand_66_out, nand_68_out);
  nand nand_66 (nand_66_out, ~in_3, ~in_5);  // NAND_Gate
  nand nand_67 (nand_67_out, ~in_5, in_3);  // NAND_Gate
  nand nand_68 (nand_68_out, nand_67_out, nand_65_out);
  nand nand_69 (nand_69_out, nand_76_out, nand_70_out);
  nand nand_70 (nand_70_out, nand_78_out, in_8);
  nand nand_71 (nand_71_out, nand_78_out, nand_72_out);
  nand nand_72 (nand_72_out, ~or_2_out, ~in_8);  // NAND_Gate
  nand nand_73 (nand_73_out, out_11, nand_74_out);
  nand nand_74 (nand_74_out, nand_68_out, in_5);
  nand nand_75 (nand_75_out, in_5, ~nand_68_out);  // NAND_Gate
  nand nand_76 (nand_76_out, nand_69_out, nand_77_out, ~in_7);  // NAND_Gate
  nand nand_77 (nand_77_out, in_8, ~nand_78_out);  // NAND_Gate
  nand nand_78 (nand_78_out, nand_71_out, nand_79_out);
  nand nand_79 (nand_79_out, ~in_8, or_2_out);  // NAND_Gate
  or or_2 (or_2_out, nand_130_out, in_9);
  nand nand_80 (out_11, nand_73_out, ~in_4, nand_75_out);  // NAND_Gate
  nand nand_81 (nand_81_out, nand_82_out, nand_83_out, ~in_7);  // NAND_Gate
  nand nand_82 (nand_82_out, nand_81_out, nand_84_out);
  nand nand_83 (nand_83_out, in_8, ~nand_91_out);  // NAND_Gate
  nand nand_84 (nand_84_out, nand_91_out, in_8);
  nand nand_85 (nand_85_out, nand_91_out, nand_87_out);
  nand nand_86 (nand_86_out, ~in_8, nand_69_out);  // NAND_Gate
  nand nand_87 (nand_87_out, ~nand_69_out, ~in_8);  // NAND_Gate
  nand nand_88 (nand_88_out, nand_93_out, nand_89_out);
  nand nand_89 (nand_89_out, nand_95_out, in_8);
  nand nand_90 (nand_90_out, nand_95_out, nand_92_out);
  nand nand_91 (nand_91_out, nand_85_out, nand_86_out);
  nand nand_92 (nand_92_out, ~nand_82_out, ~in_8);  // NAND_Gate
  nand nand_93 (nand_93_out, nand_88_out, nand_94_out, ~in_7);  // NAND_Gate
  nand nand_94 (nand_94_out, in_8, ~nand_95_out);  // NAND_Gate
  nand nand_95 (nand_95_out, nand_90_out, nand_96_out);
  nand nand_96 (nand_96_out, ~in_8, nand_82_out);  // NAND_Gate
  nand nand_97 (nand_97_out, nand_98_out, nand_100_out);
  nand nand_98 (nand_98_out, nand_97_out, nand_99_out, ~in_7);  // NAND_Gate
  nand nand_99 (nand_99_out, in_8, ~nand_107_out);  // NAND_Gate
  nand nand_100 (nand_100_out, nand_107_out, in_8);
  nand nand_101 (nand_101_out, nand_107_out, nand_103_out);
  nand nand_102 (nand_102_out, ~in_8, nand_88_out);  // NAND_Gate
  nand nand_103 (nand_103_out, ~nand_88_out, ~in_8);  // NAND_Gate
  nand nand_104 (nand_104_out, nand_109_out, nand_105_out);
  nand nand_105 (nand_105_out, nand_111_out, in_8);
  nand nand_106 (nand_106_out, nand_111_out, nand_108_out);
  nand nand_107 (nand_107_out, nand_101_out, nand_102_out);
  nand nand_108 (nand_108_out, ~nand_97_out, ~in_8);  // NAND_Gate
  nand nand_109 (nand_109_out, nand_104_out, nand_110_out, ~in_7);  // NAND_Gate
  nand nand_110 (nand_110_out, in_8, ~nand_111_out);  // NAND_Gate
  nand nand_111 (nand_111_out, nand_106_out, nand_112_out);
  nand nand_112 (nand_112_out, ~in_8, nand_97_out);  // NAND_Gate
  nand nand_113 (nand_113_out, nand_114_out, nand_115_out);
  nand nand_114 (nand_114_out, nand_113_out, nand_116_out, ~in_7);  // NAND_Gate
  nand nand_115 (nand_115_out, nand_122_out, in_8);
  nand nand_116 (nand_116_out, in_8, ~nand_122_out);  // NAND_Gate
  nand nand_117 (nand_117_out, nand_122_out, nand_118_out);
  nand nand_118 (nand_118_out, ~nand_104_out, ~in_8);  // NAND_Gate
  nand nand_119 (nand_119_out, ~in_8, nand_104_out);  // NAND_Gate
  nand nand_120 (nand_120_out, nand_125_out, nand_121_out);
  nand nand_121 (nand_121_out, nand_127_out, in_8);
  nand nand_122 (nand_122_out, nand_117_out, nand_119_out);
  nand nand_123 (nand_123_out, nand_127_out, nand_124_out);
  nand nand_124 (nand_124_out, ~nand_113_out, ~in_8);  // NAND_Gate
  nand nand_125 (nand_125_out, nand_120_out, nand_126_out, ~in_7);  // NAND_Gate
  nand nand_126 (nand_126_out, in_8, ~nand_127_out);  // NAND_Gate
  nand nand_127 (nand_127_out, nand_123_out, nand_128_out);
  nand nand_128 (nand_128_out, ~in_8, nand_113_out);  // NAND_Gate
  nand nand_129 (nand_129_out, nand_130_out, nand_131_out, ~in_7);  // NAND_Gate
  nand nand_130 (nand_130_out, nand_129_out, nand_132_out);
  nand nand_131 (nand_131_out, in_8, ~nand_136_out);  // NAND_Gate
  nand nand_132 (nand_132_out, nand_136_out, in_8);
  nand nand_133 (nand_133_out, nand_136_out, nand_134_out);
  nand nand_134 (nand_134_out, ~nand_120_out, ~in_8);  // NAND_Gate
  nand nand_135 (nand_135_out, ~in_8, nand_120_out);  // NAND_Gate
  nand nand_136 (nand_136_out, nand_133_out, nand_135_out);
endmodule

module _8bit_reg (
  input  in_1,
  input  in_2,
  input  in_3,
  input  clock,
  input  in_5,
  input  data,
  input  data_2,
  input  data_3,
  input  data_4,
  input  data_5,
  input  data_6,
  input  data_7,
  input  data_8,
  input  in_14,
  input  in_15
);

  wire and_1_out, and_2_out, and_3_out, and_4_out, and_5_out, and_6_out, and_7_out, and_8_out, and_9_out,
       and_10_out, and_11_out, and_12_out, and_13_out, and_14_out, and_15_out, and_16_out, and_17_out,
       and_18_out, and_19_out, and_20_out, controlled_buffer_1_out, controlled_buffer_2_out, nor_1_out,
       nor_2_out, nor_4_out, nor_5_out, nor_6_out, nor_7_out, nor_8_out, nor_9_out, nor_10_out, nor_11_out,
       nor_12_out, nor_13_out, nor_14_out, nor_15_out, nor_16_out, nor_17_out, nor_18_out, nor_19_out,
       nor_20_out;

  assign controlled_buffer_1_out = in_2 ? nor_1_out : 1'bz;  // Controlled_Buffer controlled_buffer_1
  Pull_Resistor pull_resistor_1 (.node(controlled_buffer_1_out));
  nor nor_1 (nor_1_out, and_1_out, nor_2_out);
  nor nor_2 (nor_2_out, nor_1_out, and_2_out);
  and and_1 (and_1_out, in_3, ~in_5);  // AND_Gate
  assign controlled_buffer_2_out = in_1 ? nor_1_out : 1'bz;  // Controlled_Buffer controlled_buffer_2
  Pull_Resistor pull_resistor_2 (.node(controlled_buffer_2_out));
  and and_2 (and_2_out, in_3, in_5);
  nor nor_3 (in_14, and_4_out, nor_4_out);
  and and_3 (and_3_out, in_15, in_14);
  nor nor_4 (nor_4_out, in_14, and_3_out);
  and and_4 (and_4_out, in_15, ~in_14);  // AND_Gate
  nor nor_5 (nor_5_out, and_5_out, nor_6_out);
  and and_5 (and_5_out, clock, ~data);  // AND_Gate
  and and_6 (and_6_out, clock, data);
  nor nor_6 (nor_6_out, nor_5_out, and_6_out);
  nor nor_7 (nor_7_out, and_8_out, nor_8_out);
  and and_7 (and_7_out, clock, data_2);
  nor nor_8 (nor_8_out, nor_7_out, and_7_out);
  and and_8 (and_8_out, clock, ~data_2);  // AND_Gate
  nor nor_9 (nor_9_out, and_9_out, nor_10_out);
  nor nor_10 (nor_10_out, nor_9_out, and_10_out);
  and and_9 (and_9_out, clock, ~data_3);  // AND_Gate
  nor nor_11 (nor_11_out, and_11_out, nor_12_out);
  and and_10 (and_10_out, clock, data_3);
  nor nor_12 (nor_12_out, nor_11_out, and_12_out);
  and and_11 (and_11_out, clock, ~data_4);  // AND_Gate
  nor nor_13 (nor_13_out, and_13_out, nor_14_out);
  and and_12 (and_12_out, clock, data_4);
  and and_13 (and_13_out, clock, ~data_5);  // AND_Gate
  and and_14 (and_14_out, clock, data_5);
  nor nor_14 (nor_14_out, nor_13_out, and_14_out);
  nor nor_15 (nor_15_out, and_16_out, nor_16_out);
  and and_15 (and_15_out, clock, data_6);
  nor nor_16 (nor_16_out, nor_15_out, and_15_out);
  and and_16 (and_16_out, clock, ~data_6);  // AND_Gate
  nor nor_17 (nor_17_out, and_17_out, nor_18_out);
  nor nor_18 (nor_18_out, nor_17_out, and_18_out);
  and and_17 (and_17_out, clock, ~data_7);  // AND_Gate
  nor nor_19 (nor_19_out, and_19_out, nor_20_out);
  and and_18 (and_18_out, clock, data_7);
  nor nor_20 (nor_20_out, nor_19_out, and_20_out);
  and and_19 (and_19_out, clock, ~data_8);  // AND_Gate
  and and_20 (and_20_out, clock, data_8);
endmodule
