// Logisim project un1.circ as structural Verilog: 8 circuits, main circuit main
module Stepper (
  input  in_1,
  input  in_2,
  output out_3,
  output out_4,
  output out_5,
  output out_6,
  output out_7,
  output out_8,
  output out_9,
  output out_10
);

  wire controlled_buffer_1_out, nor_1_out, nor_2_out, not_1_out, not_2_out;
  wire [1:0] shift_register_1_q7;

  Shift_Register shift_register_1 (
    .shift(1'b1), .in(controlled_buffer_1_out), .clk(in_1), .q0(out_3), .q1(out_4), .q2(out_5), .q3(out_6),
    .q4(out_7), .q5(out_8), .q6(shift_register_1_q7[1]), .q7(shift_register_1_q7[0]));  // open: out, load, clr, d0, d1, d2, d3, d4, d5, d6, d7
  and and_1 (out_9, in_2, shift_register_1_q7[1]);
  and and_2 (out_10, shift_register_1_q7[0], in_2);
  not not_1 (not_1_out, in_2);
  assign controlled_buffer_1_out = not_2_out ? nor_1_out : 1'bz;  // Controlled_Buffer controlled_buffer_1
  nor nor_1 (nor_1_out, shift_register_1_q7[1], out_8, out_7, out_6, out_4, out_3, out_5);
  not not_2 (not_2_out, not_1_out);
  assign controlled_buffer_1_out = not_1_out ? nor_2_out : 1'bz;  // Controlled_Buffer controlled_buffer_2
  nor nor_2 (nor_2_out, out_7, out_6, out_5, out_4, out_3);
endmodule

module main (
  input  Flag_state_in,
  input  in_2,
  input  in_3,
  input  in_4,
  input  in_5,
  input  in_6,
  input  in_7,
  input  in_8,
  input  in_9,
  output temp1,
  output out_11,
  output out_12,
  output out_13,
  output out_14,
  output out_15,
  output out_16,
  output out_17,
  output out_18,
  output out_19,
  output out_20,
  output out_21,
  output rom,
  output out_23,
  output out_24,
  output out_25
);

  wire clockbox_1_out_1, clockbox_1_out_2, demultiplexer_1_out1, nor_1_out, not_1_out, or_4_out,
       stepper_1_out_6, stepper_1_out_7, stepper_1_out_8, stepper_1_out_9, stepper_1_out_10;
  wire [8:0] demultiplexer_1_out0, demultiplexer_2_out0, demultiplexer_2_out1, or_2_out, stepper_1_out_4;
  wire [8:7] pull_resistor_1_node;

  Pull_Resistor pull_resistor_1 (.node({pull_resistor_1_node, rom, out_20, out_18, out_16, out_14, out_12, temp1}));
  assign {pull_resistor_1_node, rom, out_20, out_18, out_16, out_14, out_12, temp1} = clockbox_1_out_2 ? {or_2_out[8:5], demultiplexer_2_out1[3], or_2_out[3], demultiplexer_2_out1[2], demultiplexer_2_out1[0], or_2_out[0]} : 9'bz;  // Controlled_Buffer controlled_buffer_1
  or or_1 (or_2_out[5], stepper_1_out_10, stepper_1_out_8, stepper_1_out_6, stepper_1_out_4[0], demultiplexer_2_out1[5]);
  or or_2 (or_2_out[0], stepper_1_out_7, stepper_1_out_9);
  or or_3 (or_2_out[3], stepper_1_out_7, stepper_1_out_9, demultiplexer_2_out1[1]);
  not not_1 (not_1_out, clockbox_1_out_2);
  nor nor_1 (nor_1_out, in_2, in_3, in_4, in_5, in_6);
  clockbox clockbox_1 (.out_1(clockbox_1_out_1), .out_2(clockbox_1_out_2));
  Stepper stepper_1 (
    .out_3(or_2_out[6]), .out_4(stepper_1_out_4[0]), .out_5(stepper_1_out_4[8]), .out_6(stepper_1_out_6),
    .out_7(stepper_1_out_7), .out_8(stepper_1_out_8), .out_9(stepper_1_out_9), .out_10(stepper_1_out_10),
    .in_2(Flag_state_in), .in_1(not_1_out));
  or or_4 (or_4_out, stepper_1_out_4[8], stepper_1_out_6);
  Demultiplexer demultiplexer_1 (
    .out0(demultiplexer_1_out0[0]), .out1(demultiplexer_1_out1), .in(or_4_out), .sel(nor_1_out));  // open: en
  Decoder #(.select(3), .disabled(0)) decoder_1 (
    .out0(demultiplexer_1_out0[1]), .out1(demultiplexer_1_out0[2]), .out2(demultiplexer_1_out0[3]),
    .out3(demultiplexer_1_out0[4]), .out4(demultiplexer_1_out0[5]), .out5(demultiplexer_1_out0[6]),
    .out6(demultiplexer_1_out0[7]), .out7(demultiplexer_1_out0[8]), .sel({in_7, in_8, in_9}),
    .en(demultiplexer_1_out1));
  Demultiplexer #(.width(9)) demultiplexer_2 (
    .out0(demultiplexer_2_out0), .out1(demultiplexer_2_out1), .in(demultiplexer_1_out0),
    .sel(stepper_1_out_4[8]));  // open: en
  or or_5 (stepper_1_out_4[3], stepper_1_out_9, stepper_1_out_7, stepper_1_out_4[8], demultiplexer_2_out0[5]);
  or or_6 (stepper_1_out_4[6], stepper_1_out_8, stepper_1_out_10, demultiplexer_2_out0[1]);
  Pull_Resistor pull_resistor_2 (.node({out_25, out_24, out_23, out_21, out_19, out_17, out_15, out_13, out_11}));
  assign {out_25, out_24, out_23, out_21, out_19, out_17, out_15, out_13, out_11} = clockbox_1_out_1 ? {stepper_1_out_4[8], demultiplexer_2_out0[0], stepper_1_out_4[6], demultiplexer_2_out0[2], demultiplexer_2_out0[4], stepper_1_out_4[3], {2{or_2_out[6]}}, stepper_1_out_4[0]} : 9'bz;  // Controlled_Buffer controlled_buffer_2
endmodule

module clockbox (
  output out_1,
  output out_2
);

  wire buffer_1_out, clock_1_out, clock_2_out, not_1_out;

  Clock #(.highDuration(3), .lowDuration(3)) clock_1 (.out(clock_1_out));
  Clock clock_2 (.out(clock_2_out));
  buf buffer_1 (buffer_1_out, clock_1_out);
  not not_1 (not_1_out, clock_2_out);
  and and_1 (out_1, buffer_1_out, not_1_out);
  or or_1 (out_2, buffer_1_out, not_1_out);
endmodule

module Board (
  input  flag_in,
  input  [7:0] in_2,
  output temp,
  output temp1,
  output mar,
  output ram,
  output ir,
  output iar2,
  output acc,
  output iar,
  output out,
  output in,
  output iar2_2,
  output acc_2,
  output iar_2,
  output out_16,
  output ram_2,
  output flag
);

  main main_1 (
    .temp1(temp1), .out_12(ram), .out_14(iar2), .out_16(iar), .out_18(in), .out_20(acc_2), .rom(out_16),
    .Flag_state_in(flag_in), .out_11(temp), .out_13(mar), .out_15(ir), .out_17(acc), .out_19(out),
    .out_21(iar2_2), .out_23(iar_2), .out_24(ram_2), .out_25(flag), .in_2(in_2[7]), .in_3(in_2[6]),
    .in_4(in_2[5]), .in_5(in_2[4]), .in_6(in_2[3]), .in_7(in_2[2]), .in_8(in_2[1]), .in_9(in_2[0]));
endmodule

module enabler (
  input  in_1,
  input  in_2,
  output out_3
);

  assign out_3 = in_2 ? in_1 : 1'bz;  // Controlled_Buffer controlled_buffer_1
  Pull_Resistor pull_resistor_1 (.node(out_3));
  // AND_Gate and_1 is placed but not wired
endmodule

module CPU (
  input  [7:0] in_1,
  input  in_2,
  input  in_3,
  input  [7:0] in_4,
  output [7:0] out_5,
  output [7:0] out_6,
  output [7:0] out_7
);

  wire alu_1_carry_out, board_1_acc, board_1_flag, board_1_iar2_2, board_1_iar_2, board_1_ir, board_1_mar,
       board_1_out, board_1_ram, board_1_ram_2, board_1_temp, board_1_temp1, FLAG_q, undriven, undriven_2;
  wire [7:0] ACC_q, alu_1_c, IN_q, IR_q, MAR_q, register_1_q, temp_1_out;
  wire [15:0] IAR_q;

  Register register_1 (.D(in_1), .Q(register_1_q), .clk(in_2));  // open: en, clr
  assign in_1 = in_3 ? register_1_q : 8'bz;  // Controlled_Buffer controlled_buffer_1
  Register IAR2 (.D(out_6), .Q(IAR_q[15:8]), .clk(board_1_iar2_2));  // open: en, clr
  ALU alu_1 (.A(out_6), .B(temp_1_out), .C(alu_1_c), .carry_out(alu_1_carry_out));
  Register MAR (.D(out_6), .Q(MAR_q), .clk(board_1_mar));  // open: en, clr
  Controlled_Buffer #(.width(8)) controlled_buffer_2 (.in(IAR_q[15:8]), .out(out_6));  // open: en
  Controlled_Buffer #(.width(8)) controlled_buffer_3 (.in(ACC_q), .out(out_6));  // open: en
  Register ACC (.D(alu_1_c), .Q(ACC_q), .clk(board_1_acc));  // open: en, clr
  Temp temp_1 (.temp1(board_1_temp1), .in(out_6), .set(board_1_temp), .enable(undriven_2), .out(temp_1_out));
  Register #(.width(1)) FLAG (.D(alu_1_carry_out), .Q(FLAG_q), .clk(board_1_flag));  // open: en, clr
  Register IN (.D(in_4), .Q(IN_q), .clk(undriven));  // open: en, clr
  Controlled_Buffer #(.width(8)) controlled_buffer_4 (.in(IN_q), .out(out_6));  // open: en
  Register OUT (.D(out_6), .Q(out_7), .clk(board_1_out));  // open: en, clr
  RAM ram_1 (.addr(MAR_q), .data(out_6), .clk(board_1_ram_2), .ld(board_1_ram));  // open: sel, clr
  Register IAR (.D(out_6), .Q(IAR_q[7:0]), .clk(board_1_iar_2));  // open: en, clr
  Controlled_Buffer #(.width(8)) controlled_buffer_5 (.in(IAR_q[7:0]), .out(out_6));  // open: en
  Controlled_Buffer #(.width(8)) controlled_buffer_6 (.out(out_6));  // open: in, en
  ROM #(.addrWidth(16)) rom_1 (.addr(IAR_q));  // open: data, sel
  Board board_1 (
    .temp1(board_1_temp1), .ram(board_1_ram), .flag_in(FLAG_q), .in_2(IR_q), .temp(board_1_temp),
    .mar(board_1_mar), .ir(board_1_ir), .acc(board_1_acc), .out(board_1_out), .iar2_2(board_1_iar2_2),
    .iar_2(board_1_iar_2), .ram_2(board_1_ram_2), .flag(board_1_flag));  // open: iar2, iar, in, acc_2, out_16
  Register IR (.D(out_6), .Q(IR_q), .clk(board_1_ir));  // open: en, clr

  assign out_5 = in_1;
endmodule

module ALU (
  input  [7:0] A,
  input  [7:0] B,
  output [7:0] C,
  output carry_out
);

  Subtractor subtractor_1 (.a(A), .b(B), .out(C), .bout(carry_out));  // open: bin

  // Notes on the sheet:
  //   Note: A-B=C
endmodule

// TMP
module Temp (
  input  temp1,
  input  [7:0] in,
  input  enable,
  input  set,
  output [7:0] out
);

  wire [7:0] or_1_out, pull_resistor_1_node, register_1_q;

  Register register_1 (.D(in), .Q(register_1_q), .clk(set));  // open: en, clr
  Pull_Resistor pull_resistor_1 (.node(pull_resistor_1_node));
  assign pull_resistor_1_node = temp1 ? {8{1'b1}} : 8'bz;  // Controlled_Buffer controlled_buffer_1
  assign out = enable ? or_1_out : 8'bz;  // Controlled_Buffer controlled_buffer_2
  assign or_1_out = pull_resistor_1_node | register_1_q;  // OR_Gate or_1, 8 bits wide
endmodule
