// Logisim project un3_MAR_addition.circ as structural Verilog: 13 circuits, main circuit main
module Stepper (
  input  in_1,
  input  in_2,
  output out_3,
  output out_4,
  output out_5,
  output out_6,
  output out_7,
  output out_8
);

  wire and_1_out, and_2_out, controlled_buffer_1_out, nor_1_out, nor_2_out, not_1_out, not_2_out;
  wire [3:0] shift_register_1_q7;

  Shift_Register shift_register_1 (
    .shift(1'b1), .in(controlled_buffer_1_out), .clk(in_1), .q0(out_3), .q1(out_4), .q2(out_5), .q3(out_6),
    .q4(shift_register_1_q7[3]), .q5(shift_register_1_q7[2]), .q6(shift_register_1_q7[1]),
    .q7(shift_register_1_q7[0]));  // open: out, load, clr, d0, d1, d2, d3, d4, d5, d6, d7
  or or_1 (out_8, shift_register_1_q7[2], and_2_out);
  or or_2 (out_7, shift_register_1_q7[3], and_1_out);
  and and_1 (and_1_out, in_2, shift_register_1_q7[1]);
  and and_2 (and_2_out, shift_register_1_q7[0], in_2);
  not not_1 (not_1_out, in_2);
  assign controlled_buffer_1_out = not_2_out ? nor_1_out : 1'bz;  // Controlled_Buffer controlled_buffer_1
  nor nor_1 (nor_1_out, shift_register_1_q7[1], shift_register_1_q7[2], shift_register_1_q7[3], out_6, out_4, out_3, out_5);
  not not_2 (not_2_out, not_1_out);
  assign controlled_buffer_1_out = not_1_out ? nor_2_out : 1'bz;  // Controlled_Buffer controlled_buffer_2
  nor nor_2 (nor_2_out, shift_register_1_q7[3], out_6, out_5, out_4, out_3);
endmodule

module main (
  input  Flag_state_in,
  input  in_2,
  input  in_3,
  input  in_4,
  input  in_5,
  input  in_6,
  input  in_7,
  input  in_8,
  input  in_9,
  output acc2,
  output temp1,
  output out_12,
  output out_13,
  output out_14,
  output out_15,
  output out_16,
  output out_17,
  output out_18,
  output out_19,
  output out_20,
  output out_21,
  output out_22,
  output rom,
  output out_24,
  output out_25,
  output out_26,
  output z,
  output out_28,
  output IN_CLR,
  output MAR
);

  wire and_2_out, clockbox_1_out_2, clockbox_1_out_3, demultiplexer_1_out1, nor_1_out, not_1_out, not_2_out,
       or_3_out, stepper_1_out_6;
  wire [7:0] or_2_out;
  wire [8:0] demultiplexer_1_out0, demultiplexer_2_out0, demultiplexer_2_out1;
  wire [9:1] stepper_1_out_4;

  Pull_Resistor pull_resistor_1 (.node({z, out_25, rom, out_21, out_19, out_17, out_15, out_13, temp1}));
  assign {z, out_25, rom, out_21, out_19, out_17, out_15, out_13, temp1} = clockbox_1_out_3 ? {demultiplexer_2_out1[6], or_2_out[7:5], demultiplexer_2_out1[3], or_2_out[3], demultiplexer_2_out1[2], demultiplexer_2_out1[0], or_2_out[0]} : 9'bz;  // Controlled_Buffer controlled_buffer_1
  or or_1 (or_2_out[5], stepper_1_out_6, demultiplexer_2_out1[5], stepper_1_out_4[1]);
  and and_1 (MAR, clockbox_1_out_3, demultiplexer_2_out1[7]);
  or or_2 (or_2_out[3], or_2_out[0], demultiplexer_2_out1[1]);
  not not_1 (not_1_out, clockbox_1_out_3);
  nor nor_1 (nor_1_out, in_2, in_3, in_4, in_5, in_6);
  clockbox clockbox_1 (.out_2(clockbox_1_out_2), .out_3(clockbox_1_out_3));  // open: in_1
  Pull_Resistor pull_resistor_2 (.node(or_2_out[7]));
  Pull_Resistor pull_resistor_3 (.node(or_2_out[0]));
  Stepper stepper_1 (
    .out_3(or_2_out[6]), .out_4(stepper_1_out_4[1]), .out_5(stepper_1_out_4[9]), .out_6(stepper_1_out_6),
    .out_7(or_2_out[0]), .out_8(or_2_out[7]), .in_2(Flag_state_in), .in_1(not_1_out));
  or or_3 (or_3_out, stepper_1_out_4[9], stepper_1_out_6);
  Demultiplexer demultiplexer_1 (
    .out0(demultiplexer_1_out0[0]), .out1(demultiplexer_1_out1), .in(or_3_out), .sel(nor_1_out));  // open: en
  Decoder #(.select(3), .disabled(0)) decoder_1 (
    .out0(demultiplexer_1_out0[1]), .out1(demultiplexer_1_out0[2]), .out2(demultiplexer_1_out0[3]),
    .out3(demultiplexer_1_out0[4]), .out4(demultiplexer_1_out0[5]), .out5(demultiplexer_1_out0[6]),
    .out6(demultiplexer_1_out0[7]), .out7(demultiplexer_1_out0[8]), .sel({in_7, in_8, in_9}),
    .en(demultiplexer_1_out1));
  Demultiplexer #(.width(9)) demultiplexer_2 (
    .out0(demultiplexer_2_out0), .out1(demultiplexer_2_out1), .in(demultiplexer_1_out0),
    .sel(stepper_1_out_4[9]));  // open: en
  not not_2 (not_2_out, nor_1_out);
  or or_4 (stepper_1_out_4[7], or_2_out[7], demultiplexer_2_out0[1]);
  and and_2 (and_2_out, not_2_out, or_2_out[6]);
  or or_5 (stepper_1_out_4[2], demultiplexer_2_out0[7], and_2_out);
  Pull_Resistor pull_resistor_4 (.node({IN_CLR, out_28, out_26, out_24, out_22, out_20, out_18, out_16, out_14, out_12, acc2}));
  assign {IN_CLR, out_28, out_26, out_24, out_22, out_20, out_18, out_16, out_14, out_12, acc2} = clockbox_1_out_2 ? {demultiplexer_2_out0[3], stepper_1_out_4[9], demultiplexer_2_out0[0], stepper_1_out_4[7], demultiplexer_2_out0[2], demultiplexer_2_out0[4], stepper_1_out_4[9], or_2_out[6], stepper_1_out_4[2:1], or_2_out[0]} : 11'bz;  // Controlled_Buffer controlled_buffer_2
endmodule

module clockbox (
  input  in_1,
  output out_2,
  output out_3
);

  wire buffer_1_out, clock_1_out, clock_2_out, not_1_out, t_ff_1_q, t_ff_1_qn;

  Clock #(.highDuration(3), .lowDuration(3)) clock_1 (.out(clock_1_out));
  Clock clock_2 (.out(clock_2_out));
  T_Flip_Flop t_ff_1 (.clk(out_3), .T(in_1), .Q(t_ff_1_q), .Qn(t_ff_1_qn));  // open: preset, reset, en
  buf buffer_1 (buffer_1_out, clock_1_out);
  not not_1 (not_1_out, clock_2_out);
  and and_1 (out_2, buffer_1_out, not_1_out);
  or or_1 (out_3, buffer_1_out, not_1_out);
endmodule

module Board (
  input  flag_in,
  input  [7:0] in_2,
  output temp,
  output temp1,
  output mar,
  output ram,
  output ir,
  output iar2,
  output acc,
  output iar,
  output out,
  output in,
  output iar2_2,
  output acc_2,
  output iar_2,
  output rom,
  output ram_2,
  output acc2,
  output flag,
  output zero,
  output acc2_2,
  output mar_2,
  output IN_CLR
);

  main main_1 (
    .temp1(temp1), .out_13(ram), .out_15(iar2), .out_17(iar), .out_19(in), .out_21(acc_2), .rom(rom),
    .Flag_state_in(flag_in), .out_12(temp), .out_14(mar), .out_16(ir), .out_18(acc), .out_20(out),
    .out_22(iar2_2), .out_24(iar_2), .out_26(ram_2), .out_28(flag), .in_2(in_2[7]), .in_3(in_2[6]),
    .in_4(in_2[5]), .in_5(in_2[4]), .in_6(in_2[3]), .in_7(in_2[2]), .in_8(in_2[1]), .in_9(in_2[0]),
    .acc2(acc2_2), .out_25(acc2), .IN_CLR(IN_CLR), .z(zero), .MAR(mar_2));
endmodule

module enabler (
  input  in_1,
  input  in_2,
  output out_3
);

  assign out_3 = in_2 ? in_1 : 1'bz;  // Controlled_Buffer controlled_buffer_1
  Pull_Resistor pull_resistor_1 (.node(out_3));
  // AND_Gate and_1 is placed but not wired
endmodule

module CPU (
  input  [7:0] IN,
  input  IN_SET,
  output [7:0] OUT,
  output OUT_was_SET
);

  wire alu_1_carry_out, board_1_acc, board_1_acc2, board_1_acc2_2, board_1_acc_2, board_1_flag, board_1_iar,
       board_1_iar2, board_1_iar2_2, board_1_iar_2, board_1_in, board_1_in_clr, board_1_ir, board_1_mar,
       board_1_mar_2, board_1_ram, board_1_ram_2, board_1_rom, board_1_temp, board_1_temp1, FLAG_q;
  wire [7:0] ACC2_q, ACC_q, alu_1_c, controlled_buffer_1_out, IAR2_q, IAR_q, IN_q, IR_q, MAR_q, rom_1_data,
       temp_1_out;

  Register IAR2 (.D(controlled_buffer_1_out), .Q(IAR2_q), .clk(board_1_iar2_2));  // open: en, clr
  Register ACC2 (.D(alu_1_c), .Q(ACC2_q), .clk(board_1_acc2_2));  // open: en, clr
  assign controlled_buffer_1_out = board_1_acc2 ? ACC2_q : 8'bz;  // Controlled_Buffer controlled_buffer_1
  ALU alu_1 (.A(controlled_buffer_1_out), .B(temp_1_out), .C(alu_1_c), .carry_out(alu_1_carry_out));
  Register MAR (.D(controlled_buffer_1_out), .Q(MAR_q), .clk(board_1_mar));  // open: en, clr
  assign controlled_buffer_1_out = board_1_iar2 ? IAR2_q : 8'bz;  // Controlled_Buffer controlled_buffer_2
  ROM #(.addrWidth(16)) rom_1 (.addr({IAR2_q, IAR_q}), .data(rom_1_data));  // open: sel
  Register ACC (.D(alu_1_c), .Q(ACC_q), .clk(board_1_acc));  // open: en, clr
  assign controlled_buffer_1_out = board_1_acc_2 ? ACC_q : 8'bz;  // Controlled_Buffer controlled_buffer_3
  Temp temp_1 (.temp1(board_1_temp1), .in(controlled_buffer_1_out), .set(board_1_temp), .out(temp_1_out));
  Register #(.width(1)) FLAG (.D(alu_1_carry_out), .Q(FLAG_q), .clk(board_1_flag));  // open: en, clr
  Register u_IN (.D(IN), .Q(IN_q), .clk(IN_SET), .clr(board_1_in_clr));  // open: en
  assign controlled_buffer_1_out = board_1_in ? IN_q : 8'bz;  // Controlled_Buffer controlled_buffer_4
  Register u_OUT (.D(controlled_buffer_1_out), .Q(OUT), .clk(OUT_was_SET));  // open: en, clr
  Pull_Resistor pull_resistor_1 (.node(controlled_buffer_1_out));
  assign controlled_buffer_1_out = board_1_mar_2 ? MAR_q : 8'bz;  // Controlled_Buffer controlled_buffer_5
  RAM ram_1 (.addr(MAR_q), .data(controlled_buffer_1_out), .clk(board_1_ram_2), .ld(board_1_ram));  // open: sel, clr
  Register IAR (.D(controlled_buffer_1_out), .Q(IAR_q), .clk(board_1_iar_2));  // open: en, clr
  assign controlled_buffer_1_out = board_1_iar ? IAR_q : 8'bz;  // Controlled_Buffer controlled_buffer_6
  assign controlled_buffer_1_out = board_1_rom ? rom_1_data : 8'bz;  // Controlled_Buffer controlled_buffer_7
  Board board_1 (
    .temp1(board_1_temp1), .ram(board_1_ram), .iar2(board_1_iar2), .iar(board_1_iar), .in(board_1_in),
    .acc_2(board_1_acc_2), .rom(board_1_rom), .acc2(board_1_acc2), .temp(board_1_temp), .mar(board_1_mar),
    .ir(board_1_ir), .acc(board_1_acc), .out(OUT_was_SET), .iar2_2(board_1_iar2_2), .iar_2(board_1_iar_2),
    .ram_2(board_1_ram_2), .flag(board_1_flag), .acc2_2(board_1_acc2_2), .flag_in(FLAG_q), .in_2(IR_q),
    .IN_CLR(board_1_in_clr), .mar_2(board_1_mar_2));  // open: zero
  Register IR (.D(controlled_buffer_1_out), .Q(IR_q), .clk(board_1_ir));  // open: en, clr
  Hex_Digit_Display hex_digit_display_1 (.value(OUT[7:4]));  // open: dp
  Hex_Digit_Display hex_digit_display_2 (.value(OUT[3:0]));  // open: dp

  // Notes on the sheet:
  //   contents of rom_1 (hex, n*v repeats v):
  //   10 10 9 9 5 11 5 10 3 15*4
endmodule

module ALU (
  input  [7:0] A,
  input  [7:0] B,
  output [7:0] C,
  output carry_out
);

  Subtractor subtractor_1 (.a(A), .b(B), .out(C), .bout(carry_out));  // open: bin

  // Notes on the sheet:
  //   Note: A-B=C
endmodule

// TMP
module Temp (
  input  temp1,
  input  [7:0] in,
  input  set,
  output [7:0] out
);

  wire [7:0] pull_resistor_1_node, register_1_q;

  Register register_1 (.D(in), .Q(register_1_q), .clk(set));  // open: en, clr
  Pull_Resistor pull_resistor_1 (.node(pull_resistor_1_node));
  assign pull_resistor_1_node = temp1 ? {8{1'b1}} : 8'bz;  // Controlled_Buffer controlled_buffer_1
  assign out = pull_resistor_1_node | register_1_q;  // OR_Gate or_1, 8 bits wide
endmodule

module safe_stop (
  input  e,
  input  s,
  input  stop,
  input  e_2,
  input  s_2,
  output out_6,
  output out_7
);

  wire and_1_out, nor_1_out, or_1_out;

  Multiplexer multiplexer_1 (.in0(e), .in1(e_2), .out(out_6), .sel(and_1_out));  // open: en
  nor nor_1 (nor_1_out, e, s);
  and and_1 (and_1_out, stop, or_1_out);
  or or_1 (or_1_out, nor_1_out, and_1_out);
  Multiplexer multiplexer_2 (.in0(s), .in1(s_2), .out(out_7), .sel(and_1_out));  // open: en
endmodule

module panel (
  input  [7:0] switch_register,
  input  set_in,
  input  halt,
  input  [2:0] ereg,
  input  [2:0] sreg,
  input  set,
  input  step,
  output [7:0] DATA_OUT,
  output [5:0] Step_2,
  output [7:0] BUS_MAR_MAR2
);

  wire demultiplexer_1_out8, demultiplexer_1_out9, demultiplexer_1_out10, demultiplexer_1_out11,
       demultiplexer_1_out12, demultiplexer_1_out13, demultiplexer_1_out14, demultiplexer_1_out15,
       demultiplexer_2_out8, demultiplexer_2_out9, demultiplexer_2_out10, demultiplexer_2_out11,
       demultiplexer_2_out12, demultiplexer_2_out13, demultiplexer_2_out14, demultiplexer_2_out15;
  wire [1:0] demultiplexer_1_out6;
  wire [3:0] register_1_q;
  wire [5:0] demultiplexer_1_out0;
  wire [7:0] demultiplexer_2_out0, undriven, undriven_2, undriven_3;

  Demultiplexer #(.select(4)) demultiplexer_1 (
    .out0(demultiplexer_1_out0[0]), .out1(demultiplexer_1_out0[1]), .out2(demultiplexer_1_out0[2]),
    .out3(demultiplexer_1_out0[3]), .out4(demultiplexer_1_out0[4]), .out5(demultiplexer_1_out0[5]),
    .out6(demultiplexer_1_out6[0]), .out7(demultiplexer_1_out6[1]), .out8(demultiplexer_1_out8),
    .out9(demultiplexer_1_out9), .out10(demultiplexer_1_out10), .out11(demultiplexer_1_out11),
    .out12(demultiplexer_1_out12), .out13(demultiplexer_1_out13), .out14(demultiplexer_1_out14),
    .out15(demultiplexer_1_out15), .in(1'b1), .sel({1'b0, ereg}));  // open: en
  Multiplexer #(.select(2), .width(8)) multiplexer_1 (
    .in0(undriven), .in1(undriven_2), .in2(undriven_3), .out(BUS_MAR_MAR2), .sel(demultiplexer_1_out6));  // open: in3, en
  Demultiplexer #(.select(4)) demultiplexer_2 (
    .out0(demultiplexer_2_out0[0]), .out1(demultiplexer_2_out0[1]), .out2(demultiplexer_2_out0[2]),
    .out3(demultiplexer_2_out0[3]), .out4(demultiplexer_2_out0[4]), .out5(demultiplexer_2_out0[5]),
    .out6(demultiplexer_2_out0[6]), .out7(demultiplexer_2_out0[7]), .out8(demultiplexer_2_out8),
    .out9(demultiplexer_2_out9), .out10(demultiplexer_2_out10), .out11(demultiplexer_2_out11),
    .out12(demultiplexer_2_out12), .out13(demultiplexer_2_out13), .out14(demultiplexer_2_out14),
    .out15(demultiplexer_2_out15), .in(1'b1), .sel(register_1_q));  // open: en
  Register #(.width(4)) register_1 (.D({1'b0, sreg}), .Q(register_1_q), .clk(set));  // open: en, clr

  // Notes on the sheet:
  //   22
  //   40
  //   18
  //   47 connections
  //   25 in , 22 out
  //   38
  //   63
  //   25
endmodule

module step (
  input  in_1,
  input  in_2,
  input  in_3,
  input  in_4,
  input  in_5,
  input  stop,
  input  e,
  input  s,
  output out_9,
  output out_10,
  output out_11,
  output out_12
);

  wire and_1_out, clock_1_out, controlled_buffer_1_out, j_k_ff_1_q, nor_1_out, not_1_out, or_1_out,
       register_1_q, t_ff_1_q;

  assign controlled_buffer_1_out = in_1 ? in_1 : 1'bz;  // Controlled_Buffer controlled_buffer_1
  Clock clock_1 (.out(clock_1_out));
  assign controlled_buffer_1_out = not_1_out ? clock_1_out : 1'bz;  // Controlled_Buffer controlled_buffer_2
  not not_1 (not_1_out, in_3);
  T_Flip_Flop t_ff_1 (.clk(controlled_buffer_1_out), .T(1'b1), .Q(t_ff_1_q));  // open: Qn, preset, reset, en
  Multiplexer multiplexer_1 (.in0(out_10), .in1(e), .out(out_11), .sel(and_1_out));  // open: en
  Pull_Resistor pull_resistor_1 (.node(controlled_buffer_1_out));
  nand nand_1 (out_10, controlled_buffer_1_out, t_ff_1_q);
  Pull_Resistor pull_resistor_2 (.node(out_9));
  assign out_9 = out_10 ? controlled_buffer_1_out : 1'bz;  // Controlled_Buffer controlled_buffer_3
  nor nor_1 (nor_1_out, out_10, out_9);
  or or_1 (or_1_out, nor_1_out, register_1_q);
  and and_1 (and_1_out, stop, or_1_out);
  Multiplexer multiplexer_2 (.in0(out_9), .in1(s), .out(out_12), .sel(and_1_out));  // open: en
  Register #(.width(1)) register_1 (.D(and_1_out), .Q(register_1_q), .clk(and_1_out));  // open: en, clr
  J_K_Flip_Flop j_k_ff_1 (.J(in_2), .clk(in_2), .K(in_4), .Q(j_k_ff_1_q), .en(in_5));  // open: Qn, preset, reset
endmodule

module clock (
  input  in_1,
  input  in_2,
  input  in_3,
  input  in_4,
  output out_5,
  output out_6
);

  wire and_1_out, buffer_1_out, buffer_2_out, clock_1_out, controlled_buffer_1_out, n8_1_out_2, not_1_out,
       pull_resistor_2_node, t_ff_1_q, t_ff_1_qn, t_ff_2_qn, t_ff_3_q, t_ff_4_qn, xnor_1_out;

  xnor xnor_1 (xnor_1_out, in_1, t_ff_3_q);
  assign controlled_buffer_1_out = xnor_1_out ? clock_1_out : 1'bz;  // Controlled_Buffer controlled_buffer_1
  Clock clock_1 (.out(clock_1_out));
  Pull_Resistor pull_resistor_1 (.node(controlled_buffer_1_out));
  T_Flip_Flop t_ff_1 (
    .clk(controlled_buffer_1_out), .T(1'b1), .Q(t_ff_1_q), .Qn(t_ff_1_qn));  // open: preset, reset, en
  T_Flip_Flop t_ff_2 (.clk(t_ff_1_qn), .T(1'b1), .Qn(t_ff_2_qn));  // open: Q, preset, reset, en
  T_Flip_Flop t_ff_3 (.clk(t_ff_2_qn), .T(1'b1), .Q(t_ff_3_q));  // open: Qn, preset, reset, en
  Pull_Resistor pull_resistor_2 (.node(pull_resistor_2_node));
  assign pull_resistor_2_node = t_ff_1_q ? t_ff_1_q : 1'bz;  // Controlled_Buffer controlled_buffer_2
  not not_1 (not_1_out, in_2);
  assign pull_resistor_2_node = not_1_out ? clock_1_out : 1'bz;  // Controlled_Buffer controlled_buffer_3
  assign pull_resistor_2_node = n8_1_out_2 ? n8_1_out_2 : 1'bz;  // Controlled_Buffer controlled_buffer_4
  _8 u_8_1 (.in_1(in_3), .out_2(n8_1_out_2));
  buf buffer_1 (buffer_1_out, buffer_2_out);
  buf buffer_2 (buffer_2_out, pull_resistor_2_node);
  T_Flip_Flop t_ff_4 (.clk(pull_resistor_2_node), .T(1'b1), .Qn(t_ff_4_qn));  // open: Q, preset, reset, en
  buf buffer_3 (out_5, buffer_1_out);
  nand nand_1 (out_6, buffer_1_out, t_ff_4_qn);
  Counter counter_1 (.count(1'b1), .clk(and_1_out), .clr(in_4));  // open: load, D, Q, carry
  and and_1 (and_1_out, out_5, out_6);
endmodule

module _8 (
  input  in_1,
  output out_2
);

  wire clock_1_out, controlled_buffer_1_out, t_ff_1_qn, t_ff_2_qn, t_ff_3_qn, t_ff_4_qn, t_ff_5_qn, t_ff_6_q,
       xnor_1_out;

  xnor xnor_1 (xnor_1_out, in_1, t_ff_6_q);
  Clock clock_1 (.out(clock_1_out));
  assign controlled_buffer_1_out = xnor_1_out ? clock_1_out : 1'bz;  // Controlled_Buffer controlled_buffer_1
  Pull_Resistor pull_resistor_1 (.node(controlled_buffer_1_out));
  T_Flip_Flop t_ff_1 (.clk(controlled_buffer_1_out), .T(1'b1), .Q(out_2), .Qn(t_ff_1_qn));  // open: preset, reset, en
  T_Flip_Flop t_ff_2 (.clk(t_ff_1_qn), .T(1'b1), .Qn(t_ff_2_qn));  // open: Q, preset, reset, en
  T_Flip_Flop t_ff_3 (.clk(t_ff_2_qn), .T(1'b1), .Qn(t_ff_3_qn));  // open: Q, preset, reset, en
  T_Flip_Flop t_ff_4 (.clk(t_ff_3_qn), .T(1'b1), .Qn(t_ff_4_qn));  // open: Q, preset, reset, en
  T_Flip_Flop t_ff_5 (.clk(t_ff_4_qn), .T(1'b1), .Qn(t_ff_5_qn));  // open: Q, preset, reset, en
  T_Flip_Flop t_ff_6 (.clk(t_ff_5_qn), .T(1'b1), .Q(t_ff_6_q));  // open: Qn, preset, reset, en
endmodule
